# Fritzing sketch bme280_fritzing (saved by Fritzing 0.9.3b)
breadboards: 1

parts:
  Raspberry_Pi_Zero1 = Raspberry Pi Zero
  Part1 = BME280 Breakout

nets:
  3V3: Raspberry_Pi_Zero1.3v3, Part1.3.3V
  N1: Raspberry_Pi_Zero1.GPIO2, Part1.SDI/SDA
  N2: Raspberry_Pi_Zero1.GPIO3, Part1.SCK/SCL
  GND: Raspberry_Pi_Zero1.GND, Part1.GND
