# Fritzing sketch fritzing_led_blink (saved by Fritzing 0.9.3b)
breadboards: 1

parts:
  Raspberry_Pi_Zero1 = Raspberry Pi Zero
  LED1 = smd LED [color="Red (633nm)" package="0603 [SMD]"]
  R1 = Resistor [tolerance=±5% resistance=220 package="1206 [SMD]"]

nets:
  N1: Raspberry_Pi_Zero1.GPIO7, R1.Pin_1
  N2: Raspberry_Pi_Zero1.GND, LED1.cathode
  N3: LED1.anode, R1.Pin_0
